// Logisim project 1.circ as structural Verilog: 1 circuit, main circuit main
module main (
);

  wire and_1_out, and_2_out, and_3_out, and_4_out, and_5_out, and_6_out, and_7_out, and_8_out, and_9_out,
       and_10_out, n7408_1_pin6, n7408_1_pin8, n7408_2_pin3, n7408_2_pin8, n7408_3_pin3, n7408_3_pin6,
       n7432_2_p4, n7432_3_p4, n7486_1_pin1, n7486_1_pin2, n7486_1_pin3, n7486_1_pin4, n7486_1_pin5,
       n7486_1_pin6, n7486_1_pin8, n7486_1_pin10, n7486_2_pin1, n7486_2_pin2, n7486_2_pin3, n7486_2_pin6,
       n7486_3_pin1, n7486_3_pin2, n7486_3_pin3, n7486_3_pin6, nand_1_out, nand_2_out, nand_3_out,
       nand_4_out, nand_5_out, nand_6_out, nand_7_out, nand_8_out, nand_9_out, nand_10_out, nand_11_out,
       nand_12_out, nand_13_out, or_1_out, or_2_out, or_3_out, or_4_out, xor_1_out, xor_2_out, xor_3_out,
       xor_4_out, xor_5_out, xor_6_out, xor_7_out, xor_8_out, xor_9_out, xor_10_out;

  xor xor_1 (xor_1_out, 1'b1, 1'b1);
  and and_1 (and_1_out, 1'b1, 1'b1);
  xor xor_2 (xor_2_out, 1'b1, 1'b1);
  xor xor_3 (xor_3_out, 1'b1, 1'b0);
  xor xor_4 (xor_4_out, 1'b1, 1'b0);
  xor xor_5 (xor_5_out, 1'b1, 1'b0);
  LED led_1 (.in(xor_1_out));
  LED led_2 (.in(and_1_out));
  and and_2 (and_2_out, 1'b1, 1'b1);
  xor xor_6 (xor_6_out, 1'b0, 1'b1);
  LED led_3 (.in(xor_6_out));
  and and_3 (and_3_out, 1'b1, 1'b0);
  and and_4 (and_4_out, 1'b1, 1'b0);
  and and_5 (and_5_out, 1'b1, 1'b0);
  and and_6 (and_6_out, 1'b1, 1'b0);
  nand nand_1 (nand_1_out, 1'b1, nand_3_out);
  xor xor_7 (xor_7_out, xor_2_out, 1'b1);
  and and_7 (and_7_out, xor_2_out, 1'b1);
  xor xor_8 (xor_8_out, xor_3_out, and_3_out);
  and and_8 (and_8_out, xor_3_out, and_3_out);
  xor xor_9 (xor_9_out, xor_4_out, or_2_out);
  and and_9 (and_9_out, xor_4_out, or_2_out);
  and and_10 (and_10_out, xor_5_out, or_3_out);
  nand nand_2 (nand_2_out, 1'b1, nand_1_out);
  nand nand_3 (nand_3_out, nand_1_out, nand_3_out);
  LED led_4 (.in(xor_7_out));
  LED led_5 (.in(or_1_out));
  or or_1 (or_1_out, and_7_out, and_2_out);
  LED led_6 (.in(xor_8_out));
  or or_2 (or_2_out, and_8_out, and_4_out);
  LED led_7 (.in(xor_9_out));
  or or_3 (or_3_out, and_9_out, and_5_out);
  xor xor_10 (xor_10_out, xor_5_out, or_3_out);
  LED led_8 (.in(xor_10_out));
  LED led_9 (.in(or_4_out));
  or or_4 (or_4_out, and_10_out, and_6_out);
  nand nand_4 (nand_4_out, nand_2_out, nand_3_out);
  LED led_10 (.in(nand_3_out));
  // Digital_Oscilloscope digital_oscilloscope_1: pin names not known; wires that end beside it: 1'b1, nand_3_out, nand_4_out
  LED Y0 (.in(n7486_1_pin3));
  nand nand_5 (nand_5_out, 1'b1, 1'b1);
  _7486 u_7486_1 (
    .pin1(n7486_1_pin1), .pin2(n7486_1_pin2), .pin3(n7486_1_pin3), .pin4(n7486_1_pin4), .pin5(n7486_1_pin5),
    .pin6(n7486_1_pin6), .pin10(n7486_1_pin10), .pin9(n7486_1_pin6), .pin8(n7486_1_pin8));  // open: pin13, pin12, pin11
  _7408 u_7408_1 (
    .pin1(n7486_1_pin1), .pin2(n7486_1_pin2), .pin3(n7486_1_pin10), .pin4(n7486_1_pin4), .pin5(n7486_1_pin5),
    .pin6(n7408_1_pin6), .pin10(n7486_1_pin6), .pin9(n7486_1_pin10), .pin8(n7408_1_pin8));  // open: pin13, pin12, pin11
  // _7432 7432_1: pin names not known; wires that end beside it: 1'b1, n7408_1_pin6, n7408_1_pin8, 1'b0
  _7486 u_7486_2 (
    .pin1(n7486_2_pin1), .pin2(n7486_2_pin2), .pin3(n7486_2_pin3), .pin4(n7486_2_pin3), .pin5(n7408_1_pin8),
    .pin6(n7486_2_pin6));  // open: pin13, pin12, pin11, pin10, pin9, pin8
  _7408 u_7408_2 (
    .pin1(n7486_2_pin1), .pin2(n7486_2_pin2), .pin3(n7408_2_pin3), .pin10(n7408_1_pin8), .pin9(n7486_2_pin3),
    .pin8(n7408_2_pin8));  // open: pin4, pin5, pin6, pin13, pin12, pin11
  // _7432 7432_2: pin names not known; wires that end beside it: 1'b1, n7408_2_pin3, n7408_2_pin8, n7432_2_p4, 1'b0
  _7486 u_7486_3 (
    .pin1(n7486_3_pin1), .pin2(n7486_3_pin2), .pin3(n7486_3_pin3), .pin4(n7486_3_pin3), .pin5(n7432_2_p4),
    .pin6(n7486_3_pin6));  // open: pin13, pin12, pin11, pin10, pin9, pin8
  _7408 u_7408_3 (
    .pin1(n7486_3_pin1), .pin2(n7486_3_pin2), .pin3(n7408_3_pin3), .pin4(n7486_3_pin3), .pin5(n7432_2_p4),
    .pin6(n7408_3_pin6));  // open: pin13, pin12, pin11, pin10, pin9, pin8
  // _7432 7432_3: pin names not known; wires that end beside it: n7408_2_pin3, n7408_3_pin3, n7408_3_pin6, n7432_3_p4, n7408_2_pin8
  nand nand_6 (nand_6_out, 1'b1, nand_5_out);
  nand nand_7 (nand_7_out, nand_5_out, 1'b1);
  nand nand_8 (nand_8_out, nand_6_out, nand_7_out);
  nand nand_9 (nand_9_out, 1'b1, nand_8_out);
  nand nand_10 (nand_10_out, 1'b1, nand_9_out);
  nand nand_11 (nand_11_out, nand_9_out, nand_8_out);
  LED Y1 (.in(n7486_1_pin8));
  LED Y2 (.in(n7486_2_pin6));
  LED Y3 (.in(n7486_3_pin6));
  LED Carry (.in(n7432_3_p4));
  nand nand_12 (nand_12_out, nand_10_out, nand_7_out);
  nand nand_13 (nand_13_out, nand_10_out, nand_11_out);
  LED led_11 (.in(nand_13_out));
  LED led_12 (.in(nand_12_out));
  // also tied to GND on the sheet: {n7486_1_pin1, n7486_2_pin2, n7486_3_pin2, n7486_1_pin5}
  // also tied to VCC on the sheet: {nand_3_out, n7486_2_pin1, n7486_3_pin1, n7486_1_pin2, n7486_1_pin4}
endmodule
